# Fritzing sketch esp32_pumpkin (saved by Fritzing 1.0.4)
perfboards: 2

parts:
  A1 = Werner Rothschopf (modified to ESP32-S3-DevKitC dual USB by vanepp Aug 2024)
  A2 = Pcm5102A module
  S1 = Pushbutton [package="[THT]"]
  12V_in = Terminal 2pin
  12V_conv = Terminal 2pin
  12V_to_amp = Terminal 2pin
  5V_in = Terminal 2pin
  R1 = Resistor [tolerance=±5% resistance=220 package="0805 [SMD]"]
  Servo_1 = Header 3 [package=molex-1x3_lock]
  Servo_2 = Header 3 [package=molex-1x3_lock]
  LED_Strip = Header 3 [package=molex-1x3_lock]
  R2 = Resistor [tolerance=±5% resistance=220 package="0805 [SMD]"]
  R3 = Resistor [tolerance=±5% resistance=220 package="0805 [SMD]"]
  Audio_out2 = Header 2 [package=molex-1x2_lock]
  Audio_out1 = Header 2 [package=molex-1x2_lock]
  J1 = female pin header, 9 pins [form="♀ (female)"]
  JP1 = Header 1 [package=1x01_offset]

nets:
  3.3V: A1.Pin_1, A1.Pin_2, A2.Pin_6, A2.Pin_13, J1.pin1, JP1.1
  N1: A1.Pin_9, A2.Pin_2
  N2: A1.Pin_10, A2.Pin_4
  N3: A1.Pin_11, A2.Pin_3
  N4: A1.Pin_15, J1.pin8
  N5: A1.Pin_16, J1.pin6
  N6: A1.Pin_17, J1.pin5
  N7: A1.Pin_18, J1.pin3
  N8: A1.Pin_19, J1.pin4
  N9: A1.Pin_20, J1.pin7
  5V: A1.Pin_21, 5V_in.pin_1, Servo_1.3, Servo_2.3, LED_Strip.3
  GND: A1.Pin_22, A1.Pin_23, A1.Pin_24, A1.Pin_44, A2.Pin_1, A2.Pin_5, S1.Pin_1, S1.Pin_2, 12V_in.pin_2, 12V_conv.pin_2, 12V_to_amp.pin_2, 5V_in.pin_2, Servo_1.1, Servo_2.1, LED_Strip.1, J1.pin2
  N10: A1.Pin_27, S1.Pin_3, S1.Pin_4
  N11: A1.Pin_35, R2.Pin_1
  N12: A1.Pin_38, R3.Pin_1
  N13: A1.Pin_41, R1.Pin_1
  N14: A2.Pin_7, Audio_out2.2
  N15: A2.Pin_8, A2.Pin_10, Audio_out2.1, Audio_out1.1
  N16: A2.Pin_9, Audio_out1.2
  12V: 12V_in.pin_1, 12V_conv.pin_1, 12V_to_amp.pin_1
  N17: R1.Pin_0, LED_Strip.2
  N18: Servo_1.2, R2.Pin_0
  N19: Servo_2.2, R3.Pin_0

notes:
  12V in
  12V amp
  12V Conv
  5V in

custom parts:
  Werner Rothschopf (modified to ESP32-S3-DevKitC dual USB by vanepp Aug 2024): ESP32-S3 ESP32-S3-DevKitC-1 Dual USB development board Pyboard CircuitPython Micropython wifi BLE5.0 ESP32-S3.
  Pcm5102A module: Interface I2S PCM5102A DAC Decoder GY-PCM5102 I2S Player Module for Raspberry Pi pHAT Format Board Digital PCM5102 Audio Board.
  Terminal 2pin: 2-pin Terminal Block
